// Logisim project ALU.circ as structural Verilog
module my_adder (
  input  A,
  input  B,
  output SUM,
  output CARRY
);

  xor xor_1 (SUM, A, B);
  and and_1 (CARRY, A, B);
endmodule

module full_adder (
  input  A,
  input  B,
  input  CIN,
  output SUM,
  output COUT
);

  wire and_1_out, and_2_out, xor_1_out;

  xor xor_1 (xor_1_out, A, B);
  and and_1 (and_1_out, A, B);
  and and_2 (and_2_out, xor_1_out, CIN);
  xor xor_2 (SUM, xor_1_out, CIN);
  or or_1 (COUT, and_2_out, and_1_out);
endmodule
